# Fritzing sketch BufferBoard-1 (saved by Fritzing 0.9.5d)
breadboards: 1

parts:
  IC1 = IC, DIP package, 18 pins [chip_label=TBD62083APG]
  IC2 = IC, DIP package, 18 pins [chip_label=TBD62083APG]
  IC3 = IC, DIP package, 18 pins [chip_label=TBD62083APG]
  IC4 = IC, DIP package, 18 pins [chip_label=TBD62083APG]
  IC5 = IC, DIP package, 16 pins [chip_label="Resistor Array"]
  IC7 = IC, DIP package, 16 pins [chip_label="Resistor Array"]
  IC8 = IC, DIP package, 16 pins [chip_label="Resistor Array"]
  IC10 = IC, DIP package, 16 pins [chip_label="Resistor Array"]
  J9 = Screw terminal - 2 pins [package=THT]
  J10 = screw terminal, 9 pins
  J11 = screw terminal, 9 pins
  J12 = screw terminal, 9 pins
  J13 = screw terminal, 9 pins
  J14 = Generic shrouded header - 10 pins -- Corrected Pin Numbering [form="♂ (shrouded male)" package=THT]
  J15 = Generic shrouded header - 10 pins -- Corrected Pin Numbering [form="♂ (shrouded male)" package=THT]
  J16 = Generic shrouded header - 10 pins -- Corrected Pin Numbering [form="♂ (shrouded male)" package=THT]
  J17 = Generic shrouded header - 10 pins -- Corrected Pin Numbering [form="♂ (shrouded male)" package=THT]
  J18 = screw terminal, 9 pins
  J19 = screw terminal, 9 pins
  IC11 = IC, DIP package, 16 pins [chip_label="Resistor Array"]
  IC12 = IC, DIP package, 16 pins [chip_label="Resistor Array"]
  IC13 = IC, DIP package, 18 pins [chip_label=TBD62083APG]
  IC14 = IC, DIP package, 18 pins [chip_label=TBD62083APG]
  J20 = Screw terminal - 2 pins [package=THT]
  J21 = Generic shrouded header - 10 pins -- Corrected Pin Numbering [form="♂ (shrouded male)" package=THT]
  J22 = Generic shrouded header - 10 pins -- Corrected Pin Numbering [form="♂ (shrouded male)" package=THT]
  J23 = Generic shrouded header - 10 pins -- Corrected Pin Numbering [form="♂ (shrouded male)" package=THT]
  C1 = Ceramic Capacitor [capacitance=100nF package="100 mil [THT, multilayer]"]
  IC15 = IC, DIP package, 14 pins [chip_label=74AHCT00]
  R1 = Resistor [tolerance=±5% resistance=10k package=THT]
  R2 = Resistor [tolerance=±5% resistance=10k package=THT]
  R4 = Resistor [tolerance=±5% resistance=10k package=THT]
  R5 = Resistor [tolerance=±5% resistance=10k package=THT]
  R6 = Resistor [tolerance=±5% resistance=10k package=THT]
  J24 = screw terminal, 7 pins
  R7 = Resistor [tolerance=±5% resistance=10k package=THT]

nets:
  N1: IC1.pin1, J14.pin10
  N2: IC1.pin2, J14.pin9
  N3: IC1.pin3, J14.pin8
  N4: IC1.pin4, J14.pin7
  N5: IC1.pin5, J14.pin4
  N6: IC1.pin6, J14.pin3
  N7: IC1.pin7, J14.pin2
  N8: IC1.pin8, J14.pin1
  N9: IC1.pin9, IC2.pin9, IC3.pin9, IC4.pin9, J9.pin2, J14.pin5, J15.pin5, J16.pin5, J17.pin5
  N10: IC1.pin10, IC2.pin10, IC3.pin10, IC4.pin10, J9.pin1, J10.pin9, J11.pin9, J12.pin9, J13.pin9
  N11: IC1.pin11, IC5.pin8
  N12: IC1.pin12, IC5.pin7
  N13: IC1.pin13, IC5.pin6
  N14: IC1.pin14, IC5.pin5
  N15: IC1.pin15, IC5.pin4
  N16: IC1.pin16, IC5.pin3
  N17: IC1.pin17, IC5.pin2
  N18: IC1.pin18, IC5.pin1
  N19: IC2.pin1, J15.pin10
  N20: IC2.pin2, J15.pin9
  N21: IC2.pin3, J15.pin8
  N22: IC2.pin4, J15.pin7
  N23: IC2.pin5, J15.pin4
  N24: IC2.pin6, J15.pin3
  N25: IC2.pin7, J15.pin2
  N26: IC2.pin8, J15.pin1
  N27: IC2.pin11, IC8.pin8
  N28: IC2.pin12, IC8.pin7
  N29: IC2.pin13, IC8.pin6
  N30: IC2.pin14, IC8.pin5
  N31: IC2.pin15, IC8.pin4
  N32: IC2.pin16, IC8.pin3
  N33: IC2.pin17, IC8.pin2
  N34: IC2.pin18, IC8.pin1
  N35: IC3.pin1, J16.pin10
  N36: IC3.pin2, J16.pin9
  N37: IC3.pin3, J16.pin8
  N38: IC3.pin4, J16.pin7
  N39: IC3.pin5, J16.pin4
  N40: IC3.pin6, J16.pin3
  N41: IC3.pin7, J16.pin2
  N42: IC3.pin8, J16.pin1
  N43: IC3.pin11, IC7.pin8
  N44: IC3.pin12, IC7.pin7
  N45: IC3.pin13, IC7.pin6
  N46: IC3.pin14, IC7.pin5
  N47: IC3.pin15, IC7.pin4
  N48: IC3.pin16, IC7.pin3
  N49: IC3.pin17, IC7.pin2
  N50: IC3.pin18, IC7.pin1
  N51: IC4.pin1, J17.pin10
  N52: IC4.pin2, J17.pin9
  N53: IC4.pin3, J17.pin8
  N54: IC4.pin4, J17.pin7
  N55: IC4.pin5, J17.pin4
  N56: IC4.pin6, J17.pin3
  N57: IC4.pin7, J17.pin2
  N58: IC4.pin8, J17.pin1
  N59: IC4.pin11, IC10.pin8
  N60: IC4.pin12, IC10.pin7
  N61: IC4.pin13, IC10.pin6
  N62: IC4.pin14, IC10.pin5
  N63: IC4.pin15, IC10.pin4
  N64: IC4.pin16, IC10.pin3
  N65: IC4.pin17, IC10.pin2
  N66: IC4.pin18, IC10.pin1
  N67: IC5.pin9, J10.pin8
  N68: IC5.pin10, J10.pin7
  N69: IC5.pin11, J10.pin6
  N70: IC5.pin12, J10.pin5
  N71: IC5.pin13, J10.pin4
  N72: IC5.pin14, J10.pin3
  N73: IC5.pin15, J10.pin2
  N74: IC5.pin16, J10.pin1
  N75: IC7.pin9, J11.pin8
  N76: IC7.pin10, J11.pin7
  N77: IC7.pin11, J11.pin6
  N78: IC7.pin12, J11.pin5
  N79: IC7.pin13, J11.pin4
  N80: IC7.pin14, J11.pin3
  N81: IC7.pin15, J11.pin2
  N82: IC7.pin16, J11.pin1
  N83: IC8.pin9, J12.pin8
  N84: IC8.pin10, J12.pin7
  N85: IC8.pin11, J12.pin6
  N86: IC8.pin12, J12.pin5
  N87: IC8.pin13, J12.pin4
  N88: IC8.pin14, J12.pin3
  N89: IC8.pin15, J12.pin2
  N90: IC8.pin16, J12.pin1
  N91: IC10.pin9, J13.pin8
  N92: IC10.pin10, J13.pin7
  N93: IC10.pin11, J13.pin6
  N94: IC10.pin12, J13.pin5
  N95: IC10.pin13, J13.pin4
  N96: IC10.pin14, J13.pin3
  N97: IC10.pin15, J13.pin2
  N98: IC10.pin16, J13.pin1
  N99: J18.pin1, IC11.pin16
  N100: J18.pin2, IC11.pin15
  N101: J18.pin3, IC11.pin14
  N102: J18.pin4, IC11.pin13
  N103: J18.pin5, IC11.pin12
  N104: J18.pin6, IC11.pin11
  N105: J18.pin7, IC11.pin10
  N106: J18.pin8, IC11.pin9
  N107: J18.pin9, J19.pin9, IC13.pin10, IC14.pin10, J20.pin1
  N108: J19.pin1, IC12.pin16
  N109: J19.pin2, IC12.pin15
  N110: J19.pin3, IC12.pin14
  N111: J19.pin4, IC12.pin13
  N112: J19.pin5, IC12.pin12
  N113: J19.pin6, IC12.pin11
  N114: J19.pin7, IC12.pin10
  N115: J19.pin8, IC12.pin9
  N116: IC11.pin1, IC14.pin18
  N117: IC11.pin2, IC14.pin17
  N118: IC11.pin3, IC14.pin16
  N119: IC11.pin4, IC14.pin15
  N120: IC11.pin5, IC14.pin14
  N121: IC11.pin6, IC14.pin13
  N122: IC11.pin7, IC14.pin12
  N123: IC11.pin8, IC14.pin11
  N124: IC12.pin1, IC13.pin18
  N125: IC12.pin2, IC13.pin17
  N126: IC12.pin3, IC13.pin16
  N127: IC12.pin4, IC13.pin15
  N128: IC12.pin5, IC13.pin14
  N129: IC12.pin6, IC13.pin13
  N130: IC12.pin7, IC13.pin12
  N131: IC12.pin8, IC13.pin11
  N132: IC13.pin1, J22.pin10
  N133: IC13.pin2, J22.pin9
  N134: IC13.pin3, J22.pin8
  N135: IC13.pin4, J22.pin7
  N136: IC13.pin5, J22.pin4
  N137: IC13.pin6, J22.pin3
  N138: IC13.pin7, J22.pin2
  N139: IC13.pin8, J22.pin1
  N140: IC13.pin9, IC14.pin9, J20.pin2, J21.pin5, J22.pin5
  N141: IC14.pin1, J21.pin10
  N142: IC14.pin2, J21.pin9
  N143: IC14.pin3, J21.pin8
  N144: IC14.pin4, J21.pin7
  N145: IC14.pin5, J21.pin4
  N146: IC14.pin6, J21.pin3
  N147: IC14.pin7, J21.pin2
  N148: IC14.pin8, J21.pin1
  N149: J23.pin1, IC15.pin8, IC15.pin13
  N150: J23.pin2, IC15.pin2, IC15.pin6
  N151: J23.pin3, R2.Pin_0, J24.pin5
  N152: J23.pin4, R1.Pin_0, J24.pin6
  GND: J23.pin5, C1.0, IC15.pin7, J24.pin7
  3.3V: J23.pin6, C1.1, IC15.pin14, R1.Pin_1, R2.Pin_1, R4.Pin_1, R5.Pin_1, R6.Pin_1, R7.Pin_1
  N153: IC15.pin1, J24.pin1, R7.Pin_0
  N154: IC15.pin3, IC15.pin4
  N155: IC15.pin5, R4.Pin_0, J24.pin2
  N156: IC15.pin9, R6.Pin_0, J24.pin4
  N157: IC15.pin10, IC15.pin11
  N158: IC15.pin12, R5.Pin_0, J24.pin3

custom parts:
  Generic shrouded header - 10 pins -- Corrected Pin Numbering: Generic shrouded header
