# Fritzing sketch BufferBoard-2 (saved by Fritzing 0.9.5d)
breadboards: 1

parts:
  IC1 = MCP23017 I2C I/O Expander
  IC2 = MCP23017 I2C I/O Expander
  IC3 = MCP23017 I2C I/O Expander
  IC4 = MCP23017 I2C I/O Expander
  J1 = male pin header, 4 pins [form="♂ (male)"]
  R1 = Resistor [tolerance=±5% resistance=10k package=THT]
  R2 = Resistor [tolerance=±5% resistance=10k package=THT]
  R3 = Resistor [tolerance=±5% resistance=10k package=THT]
  R4 = Resistor [tolerance=±5% resistance=10k package=THT]
  C1 = Ceramic Capacitor [capacitance=0.1µF package="100 mil [THT, multilayer]"]
  C2 = Ceramic Capacitor [capacitance=0.1µF package="100 mil [THT, multilayer]"]
  C3 = Ceramic Capacitor [capacitance=0.1µF package="100 mil [THT, multilayer]"]
  C4 = Ceramic Capacitor [capacitance=0.1µF package="100 mil [THT, multilayer]"]
  IC5 = IC, DIP package, 18 pins [chip_label=TBD62083APG]
  IC6 = IC, DIP package, 18 pins [chip_label=TBD62083APG]
  IC7 = IC, DIP package, 18 pins [chip_label=TBD62083APG]
  IC8 = IC, DIP package, 18 pins [chip_label=TBD62083APG]
  IC9 = IC, DIP package, 18 pins [chip_label=TBD62083APG]
  IC10 = IC, DIP package, 18 pins [chip_label=TBD62083APG]
  IC11 = IC, DIP package, 16 pins [chip_label="Resistor Array"]
  IC12 = IC, DIP package, 16 pins [chip_label="Resistor Array"]
  IC13 = IC, DIP package, 16 pins [chip_label="Resistor Array"]
  IC14 = IC, DIP package, 16 pins [chip_label="Resistor Array"]
  IC15 = IC, DIP package, 16 pins [chip_label="Resistor Array"]
  IC16 = IC, DIP package, 16 pins [chip_label="Resistor Array"]
  J2 = screw terminal, 9 pins
  J3 = screw terminal, 9 pins
  J4 = screw terminal, 9 pins
  J5 = screw terminal, 9 pins
  J6 = Screw terminal - 2 pins [package=THT]
  J7 = screw terminal, 9 pins
  J8 = screw terminal, 9 pins
  R5 = Resistor [tolerance=±5% resistance=10k package=THT]
  R6 = Resistor [tolerance=±5% resistance=10k package=THT]
  R7 = Resistor [tolerance=±5% resistance=10k package=THT]
  C5 = Ceramic Capacitor [capacitance=0.1µF package="100 mil [THT, multilayer]"]
  IC17 = IC, DIP package, 14 pins [chip_label=74AHCT00]
  J9 = screw terminal, 7 pins

nets:
  N1: IC1.GPB0, IC5.pin1
  N2: IC1.GPB1, IC5.pin2
  N3: IC1.GPB2, IC5.pin3
  N4: IC1.GPB3, IC5.pin4
  N5: IC1.GPB4, IC5.pin5
  N6: IC1.GPB5, IC5.pin6
  N7: IC1.GPB6, IC5.pin7
  N8: IC1.GPB7, IC5.pin8
  3.3V: IC1.VDD, IC2.VDD, IC3.VDD, IC4.VDD, J1.pin1, R1.Pin_1, R2.Pin_0, R3.Pin_0, R4.Pin_0, C1.1, C2.1, C3.1, C4.1, R5.Pin_0, R6.Pin_0, R7.Pin_0, C5.0, IC17.pin14
  GND: IC1.VSS, IC1.A0, IC1.A1, IC1.A2, IC2.VSS, IC2.A1, IC2.A2, IC3.VSS, IC3.A0, IC3.A2, IC4.VSS, IC4.A2, J1.pin4, C1.0, C2.0, C3.0, C4.0, IC5.pin9, IC6.pin9, IC7.pin9, IC8.pin9, IC9.pin9, IC10.pin9, J6.pin2, C5.1, IC17.pin7, J9.pin7
  SCL: IC1.SCL, IC2.SCL, IC3.SCL, IC4.SCL, J1.pin2
  SDA: IC1.SDA, IC2.SDA, IC3.SDA, IC4.SDA, J1.pin3
  N9: IC1.RESET, IC2.A0, IC2.RESET, IC3.A1, IC3.RESET, IC4.A0, IC4.A1, IC4.RESET, R1.Pin_0
  N10: IC1.GPA0, IC8.pin1
  N11: IC1.GPA1, IC8.pin2
  N12: IC1.GPA2, IC8.pin3
  N13: IC1.GPA3, IC8.pin4
  N14: IC1.GPA4, IC8.pin5
  N15: IC1.GPA5, IC8.pin6
  N16: IC1.GPA6, IC8.pin7
  N17: IC1.GPA7, IC8.pin8
  N18: IC2.GPB0, IC7.pin1
  N19: IC2.GPB1, IC7.pin2
  N20: IC2.GPB2, IC7.pin3
  N21: IC2.GPB3, IC7.pin4
  N22: IC2.GPB4, IC7.pin5
  N23: IC2.GPB5, IC7.pin6
  N24: IC2.GPB6, IC7.pin7
  N25: IC2.GPB7, IC7.pin8
  N26: IC2.GPA0, IC6.pin1
  N27: IC2.GPA1, IC6.pin2
  N28: IC2.GPA2, IC6.pin3
  N29: IC2.GPA3, IC6.pin4
  N30: IC2.GPA4, IC6.pin5
  N31: IC2.GPA5, IC6.pin6
  N32: IC2.GPA6, IC6.pin7
  N33: IC2.GPA7, IC6.pin8
  N34: IC3.GPB0, IC10.pin1
  N35: IC3.GPB1, IC10.pin2
  N36: IC3.GPB2, IC10.pin3
  N37: IC3.GPB3, IC10.pin4
  N38: IC3.GPB4, IC10.pin5
  N39: IC3.GPB5, IC10.pin6
  N40: IC3.GPB6, IC10.pin7
  N41: IC3.GPB7, IC10.pin8
  N42: IC3.GPA0, IC9.pin1
  N43: IC3.GPA1, IC9.pin2
  N44: IC3.GPA2, IC9.pin3
  N45: IC3.GPA3, IC9.pin4
  N46: IC3.GPA4, IC9.pin5
  N47: IC3.GPA5, IC9.pin6
  N48: IC3.GPA6, IC9.pin7
  N49: IC3.GPA7, IC9.pin8
  N50: IC4.GPA4, R6.Pin_1, J9.pin6
  N51: IC4.GPA5, R5.Pin_1, J9.pin5
  N52: IC4.GPA6, IC17.pin2, IC17.pin6
  N53: IC4.GPA7, IC17.pin8, IC17.pin13
  N54: R2.Pin_1, IC17.pin9, J9.pin4
  N55: R3.Pin_1, IC17.pin12, J9.pin3
  N56: R4.Pin_1, IC17.pin5, J9.pin2
  12V: IC5.pin10, IC6.pin10, IC7.pin10, IC8.pin10, IC9.pin10, IC10.pin10, J2.pin9, J3.pin9, J4.pin9, J5.pin9, J6.pin1, J7.pin9, J8.pin9
  N57: IC5.pin11, IC11.pin8
  N58: IC5.pin12, IC11.pin7
  N59: IC5.pin13, IC11.pin6
  N60: IC5.pin14, IC11.pin5
  N61: IC5.pin15, IC11.pin4
  N62: IC5.pin16, IC11.pin3
  N63: IC5.pin17, IC11.pin2
  N64: IC5.pin18, IC11.pin1
  N65: IC6.pin11, IC13.pin8
  N66: IC6.pin12, IC13.pin7
  N67: IC6.pin13, IC13.pin6
  N68: IC6.pin14, IC13.pin5
  N69: IC6.pin15, IC13.pin4
  N70: IC6.pin16, IC13.pin3
  N71: IC6.pin17, IC13.pin2
  N72: IC6.pin18, IC13.pin1
  N73: IC7.pin11, IC12.pin8
  N74: IC7.pin12, IC12.pin7
  N75: IC7.pin13, IC12.pin6
  N76: IC7.pin14, IC12.pin5
  N77: IC7.pin15, IC12.pin4
  N78: IC7.pin16, IC12.pin3
  N79: IC7.pin17, IC12.pin2
  N80: IC7.pin18, IC12.pin1
  N81: IC8.pin11, IC15.pin8
  N82: IC8.pin12, IC15.pin7
  N83: IC8.pin13, IC15.pin6
  N84: IC8.pin14, IC15.pin5
  N85: IC8.pin15, IC15.pin4
  N86: IC8.pin16, IC15.pin3
  N87: IC8.pin17, IC15.pin2
  N88: IC8.pin18, IC15.pin1
  N89: IC9.pin11, IC14.pin8
  N90: IC9.pin12, IC14.pin7
  N91: IC9.pin13, IC14.pin6
  N92: IC9.pin14, IC14.pin5
  N93: IC9.pin15, IC14.pin4
  N94: IC9.pin16, IC14.pin3
  N95: IC9.pin17, IC14.pin2
  N96: IC9.pin18, IC14.pin1
  N97: IC10.pin11, IC16.pin8
  N98: IC10.pin12, IC16.pin7
  N99: IC10.pin13, IC16.pin6
  N100: IC10.pin14, IC16.pin5
  N101: IC10.pin15, IC16.pin4
  N102: IC10.pin16, IC16.pin3
  N103: IC10.pin17, IC16.pin2
  N104: IC10.pin18, IC16.pin1
  N105: IC11.pin9, J3.pin8
  N106: IC11.pin10, J3.pin7
  N107: IC11.pin11, J3.pin6
  N108: IC11.pin12, J3.pin5
  N109: IC11.pin13, J3.pin4
  N110: IC11.pin14, J3.pin3
  N111: IC11.pin15, J3.pin2
  N112: IC11.pin16, J3.pin1
  N113: IC12.pin9, J4.pin8
  N114: IC12.pin10, J4.pin7
  N115: IC12.pin11, J4.pin6
  N116: IC12.pin12, J4.pin5
  N117: IC12.pin13, J4.pin4
  N118: IC12.pin14, J4.pin3
  N119: IC12.pin15, J4.pin2
  N120: IC12.pin16, J4.pin1
  N121: IC13.pin9, J5.pin8
  N122: IC13.pin10, J5.pin7
  N123: IC13.pin11, J5.pin6
  N124: IC13.pin12, J5.pin5
  N125: IC13.pin13, J5.pin4
  N126: IC13.pin14, J5.pin3
  N127: IC13.pin15, J5.pin2
  N128: IC13.pin16, J5.pin1
  N129: IC14.pin9, J7.pin8
  N130: IC14.pin10, J7.pin7
  N131: IC14.pin11, J7.pin6
  N132: IC14.pin12, J7.pin5
  N133: IC14.pin13, J7.pin4
  N134: IC14.pin14, J7.pin3
  N135: IC14.pin15, J7.pin2
  N136: IC14.pin16, J7.pin1
  N137: IC15.pin9, J2.pin8
  N138: IC15.pin10, J2.pin7
  N139: IC15.pin11, J2.pin6
  N140: IC15.pin12, J2.pin5
  N141: IC15.pin13, J2.pin4
  N142: IC15.pin14, J2.pin3
  N143: IC15.pin15, J2.pin2
  N144: IC15.pin16, J2.pin1
  N145: IC16.pin9, J8.pin8
  N146: IC16.pin10, J8.pin7
  N147: IC16.pin11, J8.pin6
  N148: IC16.pin12, J8.pin5
  N149: IC16.pin13, J8.pin4
  N150: IC16.pin14, J8.pin3
  N151: IC16.pin15, J8.pin2
  N152: IC16.pin16, J8.pin1
  N153: R7.Pin_1, IC17.pin1, J9.pin1
  N154: IC17.pin3, IC17.pin4
  N155: IC17.pin10, IC17.pin11

notes:
  The grey wires will be on the foil side, not the component
  side. The MCP23017s wil be in sockets.

custom parts:
  MCP23017 I2C I/O Expander: The MCP23017 uses two i2c pins (these can be shared with other i2c devices), and in exchange gives you 16 general purpose pins. You can set each of 16 pins to be input, output, input with a pullup or open drain. There's even the ability to get an interrupt via an external pin when any of the inputs change so you don't have to keep polling the chip.
