# Fritzing sketch I2CCape (saved by Fritzing 0.9.5d)

parts:
  Part1 = Adafruit BeagleBone Proto Cape [part_number="Adafruit #572"]
  J1 = female pin header, 4 pins [form="♀ (female)"]

nets:
  N1: Part1.I2C2_SCL, J1.pin3
  N2: Part1.GND, J1.pin4
  N3: Part1.3.3V, J1.pin1
  N4: Part1.I2C2_SDA, J1.pin2

custom parts:
  Adafruit BeagleBone Proto Cape: Add some circuitry to your Beagle Bone or Beagle Bone Black with our lovely Proto Cape. If you have a 'Bone you need one of these! This PCB fits neatly on top of a Beagle Bone, without getting in the way of the Ethernet jack, and provides a breakout to both 46 pin headers - with individual numbering to keep them straight. We also threw down some strips to access the 5V and 3V power supplies as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
