# Fritzing sketch ProgTrackControl-1 (saved by Fritzing 0.9.5d)

parts:
  proto1 = Adafruit_PermaProto_1_2_Board
  J1 = male pin header, 10 pins [form="♂ (male)"]
  TC1 = TC4426 [package="DIP (Dual Inline) [THT]"]
  J2 = Screw terminal - 2 pins [package=THT]
  R1 = Resistor [tolerance=±5% resistance=1.5k package=THT]
  J3 = Screw terminal - 2 pins [package=THT]
  G2R-2-DC1 = G2R-2-DC12 [part_number=" G2R-2-DC12"]
  J4 = screw terminal, 6 pins
  proto2 = Adafruit_Permaproto_Full_sized_Board

nets:
  N1: proto1.connectorA12, proto1.connectorW12
  N2: proto1.connectorA18, proto1.connectorW18
  N3: proto1.connectorA19, proto1.connectorW19
  N4: proto1.connectorC11, proto1.connectorI19
  N5: proto1.connectorG10, proto1.connectorG13
  N6: proto1.connectorI9, proto1.connectorI11
  N7: proto1.connectorJ5, proto1.connectorZ5
  N8: proto1.connectorJ6, proto1.connectorY6
  N9: proto1.connectorJ12, proto1.connectorZ12
  N10: proto1.connectorX30, proto1.connectorZ30
  GND: J1.pin5, TC1.GND, J2.pin1
  3.3V: J1.pin6
  N11: J1.pin9, TC1.INB
  N12: J1.pin10, TC1.INA
  N13: TC1.OUTB, G2R-2-DC1.8_Coil_B
  12V: TC1.Vdd, J2.pin2, J3.pin2, G2R-2-DC1.1_Coil_A
  N14: TC1.OUTA, R1.Pin_1
  N15: R1.Pin_0, J3.pin1
  N16: G2R-2-DC1.4_N.O._1, J4.pin2
  N17: G2R-2-DC1.2_N.C._1, J4.pin4
  N18: G2R-2-DC1.3_COM_1, J4.pin6
  N19: G2R-2-DC1.6_COM_2, J4.pin5
  N20: G2R-2-DC1.7_N.C._2, J4.pin3
  N21: G2R-2-DC1.5_N.O._2, J4.pin1
  N22: proto2.connectorJ7, proto2.connectorZ7
  N23: proto2.connectorJ8, proto2.connectorY8
  N24: proto2.connectorX1, proto2.connectorZ1

custom parts:
  TC4426: Dual Power MOSFET Drivers
  G2R-2-DC12: Omron G2R-2-DC12
