# Fritzing sketch ProgTrackControl (saved by Fritzing 0.9.5d)

parts:
  J1 = male pin header, 10 pins [form="♂ (male)"]
  TC1 = TC4426 [package="DIP (Dual Inline) [THT]"]
  J2 = Screw terminal - 2 pins [package=THT]
  R1 = Resistor [tolerance=±5% resistance=1.5k package=THT]
  J3 = Screw terminal - 2 pins [package=THT]
  G2R-2-DC1 = G2R-2-DC12 [part_number=" G2R-2-DC12"]
  J4 = screw terminal, 6 pins
  proto2 = Adafruit_Permaproto_Full_sized_Board
  S1 = Toggle Switch [package=THT]
  R2 = Resistor [tolerance=±5% resistance=10k package=THT]

nets:
  N1: J1.pin1, S1.COM, R2.Pin_1
  GND: J1.pin5, TC1.GND, J2.pin1, S1.L2
  3.3V: J1.pin6, R2.Pin_0
  N2: J1.pin9, TC1.INB
  N3: J1.pin10, TC1.INA
  N4: TC1.OUTB, G2R-2-DC1.8_Coil_B
  12V: TC1.Vdd, J2.pin2, J3.pin2, G2R-2-DC1.1_Coil_A
  N5: TC1.OUTA, R1.Pin_1
  N6: R1.Pin_0, J3.pin1
  N7: G2R-2-DC1.4_N.O._1, J4.pin2
  N8: G2R-2-DC1.2_N.C._1, J4.pin4
  N9: G2R-2-DC1.3_COM_1, J4.pin6
  N10: G2R-2-DC1.6_COM_2, J4.pin5
  N11: G2R-2-DC1.7_N.C._2, J4.pin3
  N12: G2R-2-DC1.5_N.O._2, J4.pin1
  N13: proto2.connectorA14, proto2.connectorW14
  N14: proto2.connectorA23, proto2.connectorW23
  N15: proto2.connectorA31, proto2.connectorF42
  N16: proto2.connectorB29, proto2.connectorF40
  N17: proto2.connectorC33, proto2.connectorF38
  N18: proto2.connectorD13, proto2.connectorJ23
  N19: proto2.connectorE19, proto2.connectorF19
  N20: proto2.connectorF3, proto2.connectorG47
  N21: proto2.connectorF20, proto2.connectorW20
  N22: proto2.connectorF37, proto2.connectorJ33
  N23: proto2.connectorG11, proto2.connectorG13
  N24: proto2.connectorG41, proto2.connectorH31
  N25: proto2.connectorH39, proto2.connectorI29
  N26: proto2.connectorI12, proto2.connectorI15
  N27: proto2.connectorJ7, proto2.connectorZ7
  N28: proto2.connectorJ8, proto2.connectorY8
  N29: proto2.connectorJ14, proto2.connectorZ14
  N30: proto2.connectorJ46, proto2.connectorZ46
  N31: proto2.connectorX1, proto2.connectorZ1

custom parts:
  TC4426: Dual Power MOSFET Drivers
  G2R-2-DC12: Omron G2R-2-DC12
