# Fritzing sketch ProgTrackRelayHat (saved by Fritzing 0.9.5d)

parts:
  Part1 = Adafruit Perma-Proto HAT [part_number="Adafruit #2314 and #2310"]
  G2R-2-DC1 = G2R-2-DC12 [part_number=" G2R-2-DC12"]
  IC1 = IC, DIP package, 8 pins [chip_label=TC4426]
  J1 = Screw terminal - 2 pins [part_number=12V package=THT]
  J2 = Screw terminal - 2 pins [part_number="Blue LEDS" package=THT]
  R1 = Resistor [tolerance=±5% resistance=1.5k package=THT]
  J3 = Camdenboss CTB0158-3 [part_number=CTB0158-3 package=THT]
  J4 = Camdenboss CTB0158-3 [part_number=CTB0158-3 package=THT]
  S2 = Toggle Switch [package=THT]
  R3 = Resistor [tolerance=±5% resistance=10k package=THT]

nets:
  N1: Part1.GPIO4, Part1.N$59, IC1.pin4
  N2: Part1.GPIO17, Part1.N$58, IC1.pin2
  GPIO18: Part1.GPIO18, Part1.N$53, S2.COM, R3.Pin_1
  N3: Part1.GND, Part1.N$10, Part1.N$54#336, Part1.N$60, IC1.pin3, J1.pin2
  3.3V: Part1.3.3V, R3.Pin_0
  N4: Part1.N$1, J2.pin2, R1.Pin_1
  N5: Part1.N$2#161, Part1.N$4#175, Part1.N$11#208, Part1.N$49#315, G2R-2-DC1.8_Coil_B, IC1.pin6, J1.pin1, J2.pin1
  N6: Part1.N$2#162, Part1.N$4#172
  N7: Part1.N$3#166, Part1.N$13#216
  N8: Part1.N$3#170, Part1.N$13#220, G2R-2-DC1.1_Coil_A, IC1.pin5
  N9: Part1.N$4#173, Part1.N$11#209
  N10: Part1.N$5, IC1.pin7, R1.Pin_0
  N11: Part1.N$6, IC1.pin8
  N12: Part1.N$11#210, Part1.N$49#313
  N13: Part1.N$19, G2R-2-DC1.2_N.C._1, J3.pin3
  N14: Part1.N$22, G2R-2-DC1.3_COM_1, J3.pin2
  N15: Part1.N$23, G2R-2-DC1.4_N.O._1, J3.pin1
  N16: Part1.N$39, G2R-2-DC1.5_N.O._2, J4.pin3
  N17: Part1.N$42, G2R-2-DC1.6_COM_2, J4.pin2
  N18: Part1.N$44, G2R-2-DC1.7_N.C._2, J4.pin1
  N19: Part1.N$54#339, S2.L1
  GND: Part1.N$55, S2.L2
  N20: Part1.N$57, IC1.pin1

custom parts:
  Adafruit Perma-Proto HAT: To kick off the Adafruit HAT party, we have this Perma-Proto inspired plug in daughter board. It has a grid of 0.1" prototyping soldering holes for attaching chips, resistors, LED, potentiometers and more. The holes are connected underneath with traces to mimic the solderless breadboards you're familiar. There's also long power strips for +3V, +5V and Ground connections to the Pi. Near the top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
  G2R-2-DC12: Omron G2R-2-DC12
