# Fritzing sketch ESP32S3-YardLadderRouteSelector (saved by Fritzing 0.9.5d)

parts:
  switch1 = Rotary Switch 1x5
  J1 = screw terminal, 5 pins

nets:
  N1: switch1.2, J1.pin1
  N2: switch1.3, J1.pin2
  N3: switch1.4, J1.pin3
  N4: switch1.5, J1.pin4
  N5: switch1.A, J1.pin5

notes:
  GND
  4
  3
  2
  1
  Main
  Track 1
  Track 2
  Track 3
  Track 4
  Button Terminal
  Block

custom parts:
  Rotary Switch 1x5: Rotary Switch 1x5 - 1 pole 5 position - SP5T Knob arrow will point as per drawing when in position #1
