# Fritzing sketch ESP32-TTGO-T7-OctalCTSense (saved by Fritzing 0.9.5d)
perfboards: 1

parts:
  TTGO-T7_V1_4 = TTGO-T7 V1.3 [part_number=TTGO-T7-V1.3]
  J5 = Screw terminal - 2 pins [package=THT]
  J6 = Screw terminal - 2 pins [package=THT]
  D4 = Schottky Diode [part_number=SB240E package="300 mil [THT]"]
  D5 = Schottky Diode [part_number=SB240E package="300 mil [THT]"]
  D6 = Schottky Diode [part_number=SB240E package="300 mil [THT]"]
  Part5 = prefix0000
  Part6 = prefix0000
  R3 = Resistor [package=THT]
  R4 = Resistor [package=THT]
  J7 = double row male pin header, 2 pins [form="♂ (male)"]
  J8 = double row male pin header, 2 pins [form="♂ (male)"]
  C6 = Capacitor [part_number=.1nf package=axial-5mm]
  C7 = Capacitor [part_number=47nf package=axial-5mm]
  IC3 = IC, DIP package, 8 pins [chip_label=TCAN332DR]
  IC4 = IC, DIP package, 8 pins [chip_label=LM2574N-5.0]
  L2 = Inductors [package=npi75c]
  J9 = screw terminal, 8 pins
  D7 = Diode [package=diode-1n4148]
  D8 = Diode [package=diode-1n4148]
  D9 = Diode [package=diode-1n4148]
  D10 = Diode [package=diode-1n4148]
  D11 = Diode [package=diode-1n4148]
  D12 = Diode [package=diode-1n4148]
  D13 = Diode [package=diode-1n4148]
  D14 = Diode [package=diode-1n4148]
  U1 = Quad Comparator [part_number=LM339 package="DIP (Dual Inline) [THT]"]
  Part7 = Quad Comparator [part_number=LM339 package="DIP (Dual Inline) [THT]"]
  U1_1 = Quad Comparator [part_number=LM339 package="DIP (Dual Inline) [THT]"]
  U1_2 = Quad Comparator [part_number=LM339 package="DIP (Dual Inline) [THT]"]
  U1_3 = Quad Comparator [part_number=LM339 package="DIP (Dual Inline) [THT]"]
  U1_4 = Quad Comparator [part_number=LM339 package="DIP (Dual Inline) [THT]"]
  U2 = Quad Comparator [part_number=LM339 package="DIP (Dual Inline) [THT]"]
  Part8 = Quad Comparator [part_number=LM339 package="DIP (Dual Inline) [THT]"]
  U2_1 = Quad Comparator [part_number=LM339 package="DIP (Dual Inline) [THT]"]
  U2_2 = Quad Comparator [part_number=LM339 package="DIP (Dual Inline) [THT]"]
  U2_3 = Quad Comparator [part_number=LM339 package="DIP (Dual Inline) [THT]"]
  U2_4 = Quad Comparator [part_number=LM339 package="DIP (Dual Inline) [THT]"]
  R6 = Trimmer Potentiometer [maximum_resistance=10kΩ package=THT]
  R9 = Trimmer Potentiometer [maximum_resistance=10kΩ package=THT]
  R10 = Trimmer Potentiometer [maximum_resistance=10kΩ package=THT]
  R11 = Trimmer Potentiometer [maximum_resistance=10kΩ package=THT]
  C15 = Electrolytic Capacitor [package="100 mil [THT, electrolytic]"]
  C16 = Electrolytic Capacitor [package="100 mil [THT, electrolytic]"]
  C17 = Electrolytic Capacitor [package="100 mil [THT, electrolytic]"]
  C18 = Electrolytic Capacitor [package="100 mil [THT, electrolytic]"]
  C19 = Electrolytic Capacitor [package="100 mil [THT, electrolytic]"]
  C20 = Electrolytic Capacitor [package="100 mil [THT, electrolytic]"]
  C21 = Electrolytic Capacitor [package="100 mil [THT, electrolytic]"]
  R21 = 220 Ω Resistor [package=THT]
  R22 = 220 Ω Resistor [package=THT]
  R23 = 220 Ω Resistor [package=THT]
  R24 = 220 Ω Resistor [package=THT]
  R25 = 220 Ω Resistor [package=THT]
  R26 = 220 Ω Resistor [package=THT]
  R27 = 220 Ω Resistor [package=THT]
  R28 = 220 Ω Resistor [package=THT]
  R29 = 220 Ω Resistor [package=THT]
  R30 = 220 Ω Resistor [package=THT]
  R31 = 220 Ω Resistor [package=THT]
  R32 = 220 Ω Resistor [package=THT]
  LED5 = Red LED - 5mm [package="5 mm [THT]"]
  LED6 = Red LED - 5mm [package="5 mm [THT]"]
  LED7 = Red LED - 5mm [package="5 mm [THT]"]
  LED8 = Red LED - 5mm [package="5 mm [THT]"]
  R33 = 220 Ω Resistor [package=THT]
  R34 = 220 Ω Resistor [package=THT]
  R35 = 220 Ω Resistor [package=THT]
  R36 = 220 Ω Resistor [package=THT]
  R37 = 220 Ω Resistor [package=THT]
  R38 = 220 Ω Resistor [package=THT]
  R39 = 220 Ω Resistor [package=THT]
  R40 = 220 Ω Resistor [package=THT]
  R41 = 220 Ω Resistor [package=THT]
  R42 = 220 Ω Resistor [package=THT]
  R43 = 220 Ω Resistor [package=THT]
  R44 = 220 Ω Resistor [package=THT]
  C22 = Electrolytic Capacitor [package="100 mil [THT, electrolytic]"]
  C23 = Electrolytic Capacitor [package="100 mil [THT, electrolytic]"]
  C24 = Electrolytic Capacitor [package="100 mil [THT, electrolytic]"]
  C25 = Electrolytic Capacitor [package="100 mil [THT, electrolytic]"]
  J10 = screw terminal, 8 pins
  D15 = Diode [package=diode-1n4148]
  D16 = Diode [package=diode-1n4148]
  D17 = Diode [package=diode-1n4148]
  D18 = Diode [package=diode-1n4148]
  D19 = Diode [package=diode-1n4148]
  D20 = Diode [package=diode-1n4148]
  D21 = Diode [package=diode-1n4148]
  D22 = Diode [package=diode-1n4148]
  U3_4 = Quad Comparator [part_number=LM339 package="DIP (Dual Inline) [THT]"]
  U3_3 = Quad Comparator [part_number=LM339 package="DIP (Dual Inline) [THT]"]
  U3_2 = Quad Comparator [part_number=LM339 package="DIP (Dual Inline) [THT]"]
  U3_1 = Quad Comparator [part_number=LM339 package="DIP (Dual Inline) [THT]"]
  Part9 = Quad Comparator [part_number=LM339 package="DIP (Dual Inline) [THT]"]  # not connected
  U3 = Quad Comparator [part_number=LM339 package="DIP (Dual Inline) [THT]"]  # not connected
  U4_4 = Quad Comparator [part_number=LM339 package="DIP (Dual Inline) [THT]"]
  U4_3 = Quad Comparator [part_number=LM339 package="DIP (Dual Inline) [THT]"]
  U4_2 = Quad Comparator [part_number=LM339 package="DIP (Dual Inline) [THT]"]
  U4_1 = Quad Comparator [part_number=LM339 package="DIP (Dual Inline) [THT]"]
  Part10 = Quad Comparator [part_number=LM339 package="DIP (Dual Inline) [THT]"]  # not connected
  U4 = Quad Comparator [part_number=LM339 package="DIP (Dual Inline) [THT]"]  # not connected
  R45 = Trimmer Potentiometer [maximum_resistance=10kΩ package=THT]
  R46 = Trimmer Potentiometer [maximum_resistance=10kΩ package=THT]
  R47 = Trimmer Potentiometer [maximum_resistance=10kΩ package=THT]
  R48 = Trimmer Potentiometer [maximum_resistance=10kΩ package=THT]
  LED9 = Red LED - 5mm [package="5 mm [THT]"]
  LED11 = Red LED - 5mm [package="5 mm [THT]"]
  LED12 = Red LED - 5mm [package="5 mm [THT]"]
  LED13 = Red LED - 5mm [package="5 mm [THT]"]
  TC1 = TC4426 [package="DIP (Dual Inline) [THT]"]
  TC2 = TC4426 [package="DIP (Dual Inline) [THT]"]
  R49 = Resistor [tolerance=±5% resistance=220 package=THT]
  R50 = Resistor [tolerance=±5% resistance=220 package=THT]
  R51 = Resistor [tolerance=±5% resistance=220 package=THT]
  R52 = Resistor [tolerance=±5% resistance=220 package=THT]
  J11 = screw terminal, 6 pins
  U5 = SN74LS14N [package="DIP14 [THT]"]
  R53 = 220 Ω Resistor [package=THT]
  R54 = 220 Ω Resistor [package=THT]
  R55 = 220 Ω Resistor [package=THT]
  R56 = 220 Ω Resistor [package=THT]
  C26 = Capacitor [package=axial-5mm]
  C27 = Capacitor [package=axial-5mm]
  C28 = Capacitor [package=axial-5mm]
  C29 = Capacitor [package=axial-5mm]
  C30 = Capacitor [package=axial-5mm]
  J12 = screw terminal, 5 pins

nets:
  GND: TTGO-T7_V1_4.GND1, TTGO-T7_V1_4.GND2, TTGO-T7_V1_4.GND3, J5.pin2, J6.pin2, D5.anode, Part5.N$3, Part5.N$5, Part5.N$6, Part6.N$3, Part6.N$5, Part6.N$6, C6.2, C7.1, IC3.pin2, IC4.pin2, IC4.pin3, IC4.pin4, U1.connector11, Part7.pin_12, U2.connector11, Part8.pin_12, R6.leg2, R9.leg2, R10.leg2, R11.leg2, C15.-, C16.-, C17.-, C18.-, C19.-, C20.-, C21.-, C22.-, C23.-, C24.-, C25.-, R45.leg2, R46.leg2, R47.leg2, R48.leg2, TC1.GND, TC2.GND, J11.pin6, U5.GND, C26.1, C27.2, C28.2, C29.2, C30.2, J12.pin5
  LED 3: TTGO-T7_V1_4.IO_36, TC2.INA
  LED 4: TTGO-T7_V1_4.IO_39, TC2.INB
  Button 3: TTGO-T7_V1_4.IO_26, U5.3Y
  LED 2: TTGO-T7_V1_4.IO_35, TC1.INB
  OD 5: TTGO-T7_V1_4.IO_18, U4_2.pin_2, LED9.cathode
  OD 8: TTGO-T7_V1_4.IO_33, U4_3.pin_14, LED12.cathode
  OD 6: TTGO-T7_V1_4.IO_19, U4_1.pin_1, LED13.cathode
  LED 1: TTGO-T7_V1_4.IO_34, TC1.INA
  Button 1: TTGO-T7_V1_4.IO_23, U5.1Y
  CAN TX: TTGO-T7_V1_4.IO_05, IC3.pin1
  3.3V: TTGO-T7_V1_4.3V3, C6.1, IC3.pin3, U1.connector2, Part7.pin_3, U2.connector2, Part8.pin_3, C15.+, R21.Pin_0, R22.Pin_0, R23.Pin_0, R24.Pin_0, R25.Pin_0, R26.Pin_0, R27.Pin_0, R28.Pin_0, R29.Pin_0, R30.Pin_0, R31.Pin_0, R32.Pin_0, R33.Pin_0, R34.Pin_0, R35.Pin_0, R36.Pin_0, R37.Pin_0, R38.Pin_0, R39.Pin_0, R40.Pin_0, R41.Pin_0, R42.Pin_0, R43.Pin_0, R44.Pin_0, U5.VCC, R53.Pin_0, R54.Pin_0, R55.Pin_0, R56.Pin_0, C29.1
  Button 4: TTGO-T7_V1_4.IO_27, U5.4Y
  Button 2: TTGO-T7_V1_4.IO_25, U5.2Y
  OD 7: TTGO-T7_V1_4.IO_32, U4_4.pin_13, LED11.cathode
  OD 4: TTGO-T7_V1_4.IO_17, U2.connector13, U2_3.pin_14, LED8.cathode
  OD 3: TTGO-T7_V1_4.IO_16, U2.connector12, U2_4.pin_13, LED7.cathode
  CAN RX: TTGO-T7_V1_4.IO_04, IC3.pin4
  OD 1: TTGO-T7_V1_4.IO_00, U2.connector1, U2_2.pin_2, LED5.cathode
  5V: TTGO-T7_V1_4.+5V, IC4.pin1, L2.2, C21.+
  OD 2: TTGO-T7_V1_4.IO_02, U2.connector0, U2_1.pin_1, LED6.cathode
  N1: J5.pin1, D6.anode
  N2: J6.pin1, D4.cathode
  12V: D4.anode, D6.cathode, Part5.N$8, Part6.N$8, IC4.pin5, C20.+
  N3: D5.cathode, IC4.pin7, L2.1
  CAN H: Part5.N$1, Part6.N$1, R3.Pin_0, IC3.pin7
  CAN L: Part5.N$2, Part6.N$2, R4.Pin_0, IC3.pin6
  N4: Part5.N$4, Part6.N$4
  N5: Part5.N$7, Part6.N$7
  N6: R3.Pin_1, J7.pin2
  N7: R4.Pin_1, J8.pin2
  N8: J7.pin1, J8.pin1, C7.2
  N9: J9.pin1, D7.A, D8.C, U1.connector3, U1_2.pin_4
  N10: J9.pin2, D7.C, D8.A, R6.wiper
  N11: J9.pin3, D9.A, D10.C, U1.connector5, U1_1.pin_6
  N12: J9.pin4, D9.C, D10.A, R9.wiper
  N13: J9.pin5, D12.A, D13.C, U1.connector9, U1_4.pin_10#9
  N14: J9.pin6, D12.C, D13.A, R10.wiper
  N15: J9.pin7, D11.A, D14.C, U1.connector7, U1_3.pin_8
  N16: J9.pin8, D11.C, D14.A, R11.wiper
  N17: U1.connector0, U1_1.pin_1, U2.connector6, U2_1.pin_7, C17.+, R25.Pin_1
  N18: U1.connector1, U1_2.pin_2, U2.connector4, U2_2.pin_5, C16.+, R22.Pin_1
  N19: U1.connector4, U1_2.pin_5, U2.connector3, U2_2.pin_4, R6.leg1, R21.Pin_1
  N20: U1.connector6, U1_1.pin_7, U2.connector5, U2_1.pin_6, R9.leg1, R24.Pin_1
  N21: U1.connector8, U1_3.pin_9, U2.connector7, U2_3.pin_8, R11.leg1, R32.Pin_1
  N22: U1.connector10, U1_4.pin_10#10, U2.connector9, U2_4.pin_10#9, R10.leg1, R29.Pin_1
  N23: U1.connector12, U1_4.pin_13, U2.connector10, U2_4.pin_10#10, C18.+, R28.Pin_1
  N24: U1.connector13, U1_3.pin_14, U2.connector8, U2_3.pin_9, C19.+, R31.Pin_1
  N25: R23.Pin_1, LED5.anode
  N26: R26.Pin_1, LED6.anode
  N27: R27.Pin_1, LED7.anode
  N28: R30.Pin_1, LED8.anode
  N29: R33.Pin_1, U3_2.pin_5, U4_2.pin_4, R48.leg1
  N30: R34.Pin_1, C22.+, U3_2.pin_2, U4_2.pin_5
  N31: R35.Pin_1, LED9.anode
  N32: R36.Pin_1, U3_1.pin_7, U4_1.pin_6, R47.leg1
  N33: R37.Pin_1, C23.+, U3_1.pin_1, U4_1.pin_7
  N34: R38.Pin_1, LED13.anode
  N35: R39.Pin_1, LED11.anode
  N36: R40.Pin_1, C24.+, U3_4.pin_13, U4_4.pin_10#10
  N37: R41.Pin_1, U3_4.pin_10#10, U4_4.pin_10#9, R46.leg1
  N38: R42.Pin_1, LED12.anode
  N39: R43.Pin_1, C25.+, U3_3.pin_14, U4_3.pin_9
  N40: R44.Pin_1, U3_3.pin_9, U4_3.pin_8, R45.leg1
  N41: J10.pin1, D18.A, D22.C, U3_2.pin_4
  N42: J10.pin2, D18.C, D22.A, R48.wiper
  N43: J10.pin3, D17.A, D21.C, U3_1.pin_6
  N44: J10.pin4, D17.C, D21.A, R47.wiper
  N45: J10.pin5, D15.A, D20.C, U3_4.pin_10#9
  N46: J10.pin6, D15.C, D20.A, R46.wiper
  N47: J10.pin7, D16.A, D19.C, U3_3.pin_8
  N48: J10.pin8, D16.C, D19.A, R45.wiper
  N49: TC1.OUTB, R50.Pin_0
  VDD: TC1.Vdd, TC2.Vdd, J11.pin1
  N50: TC1.OUTA, R49.Pin_0
  N51: TC2.OUTB, R52.Pin_0
  N52: TC2.OUTA, R51.Pin_0
  N53: R49.Pin_1, J11.pin2
  N54: R50.Pin_1, J11.pin3
  N55: R51.Pin_1, J11.pin4
  N56: R52.Pin_1, J11.pin5
  N57: U5.1A, R53.Pin_1, C26.2, J12.pin1
  N58: U5.2A, R54.Pin_1, C27.1, J12.pin2
  N59: U5.3A, R55.Pin_1, C28.1, J12.pin3
  N60: U5.4A, U5.5A, U5.6A, R56.Pin_1, C30.1, J12.pin4

custom parts:
  Resistor: A generic 5-band resistor (0.25W)
  Quad Comparator: LM239 Quad Comparator
  Quad Comparator: LM239 Quad Comparator
  Quad Comparator: LM239 Quad Comparator
  Quad Comparator: LM239 Quad Comparator
  Quad Comparator: LM239 Quad Comparator
  Quad Comparator: LM239 Quad Comparator
  Electrolytic Capacitor: A small electrolytic capacitor
  220 Ω Resistor: A generic resistor (0.25W)
  Red LED - 5mm: A generic red LED (~1.8V)
  TC4426: Dual Power MOSFET Drivers
