# Fritzing sketch ESP32-TTGO-T7-OctalStallMotor-Prototype1 (saved by Fritzing 0.9.5d)
perfboards: 1

parts:
  J1 = Screw terminal - 2 pins [package=THT]
  J2 = Screw terminal - 2 pins [package=THT]
  D1 = Schottky Diode [part_number=SB240E package="300 mil [THT]"]
  R1 = Resistor [package=THT]
  R2 = Resistor [package=THT]
  J3 = double row male pin header, 2 pins [form="♂ (male)"]
  J4 = double row male pin header, 2 pins [form="♂ (male)"]
  C1 = Capacitor [part_number=47nf package=axial-5mm]
  IC1 = IC, DIP package, 8 pins [chip_label=TCAN332DR]
  C2 = Capacitor [part_number=.1nf package=axial-5mm]
  C3 = Electrolytic Capacitor [capacitance=1µF package="100 mil [THT, electrolytic]"]
  Part3 = prefix0000
  Part4 = prefix0000
  D2 = Schottky Diode [part_number=SB240E package="300 mil [THT]"]
  IC2 = IC, DIP package, 8 pins [chip_label=LM2574N-5.0]
  C4 = Tantalum Capacitor [capacitance=0.22mF voltage=35V package="200 mil [THT, tantalum]"]
  C5 = Tantalum Capacitor [capacitance=22µF voltage=0.1kV package="200 mil [THT, tantalum]"]
  L1 = Inductors [package=npi75c]
  D3 = Schottky Diode [part_number=SB240E package="300 mil [THT]"]
  U2 = 74HCT00 [package="DIP14 [THT]"]
  IC3 = DIP - 8 pins [chip_label=TC4428 package="DIP (Dual Inline) [THT]"]
  IC4 = DIP - 8 pins [chip_label=TC4428 package="DIP (Dual Inline) [THT]"]
  RR1 = SIP 9 Resistors [package="SIP 9"]
  J5 = screw terminal, 5 pins
  J6 = screw terminal, 5 pins
  C6 = Capacitor [package=axial-5mm]
  TTGO-T7_V1_3 = TTGO-T7 V1.3 [part_number=TTGO-T7-V1.3]
  U3 = 74HCT00 [package="DIP14 [THT]"]
  IC5 = DIP - 8 pins [chip_label=TC4428 package="DIP (Dual Inline) [THT]"]
  IC6 = DIP - 8 pins [chip_label=TC4428 package="DIP (Dual Inline) [THT]"]
  J7 = screw terminal, 5 pins
  J8 = screw terminal, 5 pins
  C7 = Capacitor [package=axial-5mm]
  U4 = 74HCT00 [package="DIP14 [THT]"]
  U5 = 74HCT00 [package="DIP14 [THT]"]
  IC7 = DIP - 8 pins [chip_label=TC4428 package="DIP (Dual Inline) [THT]"]
  IC8 = DIP - 8 pins [chip_label=TC4428 package="DIP (Dual Inline) [THT]"]
  IC9 = DIP - 8 pins [chip_label=TC4428 package="DIP (Dual Inline) [THT]"]
  IC10 = DIP - 8 pins [chip_label=TC4428 package="DIP (Dual Inline) [THT]"]
  RR2 = SIP 9 Resistors [package="SIP 9"]
  J9 = screw terminal, 5 pins
  J10 = screw terminal, 5 pins
  J11 = screw terminal, 5 pins
  J12 = screw terminal, 5 pins
  C8 = Capacitor [package=axial-5mm]
  C9 = Capacitor [package=axial-5mm]

nets:
  N1: J1.pin1, D1.cathode
  GND: J1.pin2, J2.pin2, C1.1, IC1.pin2, C2.2, C3.-, Part3.N$3, Part3.N$5, Part3.N$6, Part4.N$3, Part4.N$5, Part4.N$6, IC2.pin2, IC2.pin3, IC2.pin4, C4.-, C5.-, D3.anode, U2.GND, IC3.pin3, IC4.pin3, J5.pin4, J6.pin4, C6.2, TTGO-T7_V1_3.GND1, TTGO-T7_V1_3.GND2, TTGO-T7_V1_3.GND3, U3.GND, J7.pin4, J8.pin4, C7.2, U4.GND, U5.GND, IC7.pin3, IC8.pin3, J9.pin4, J10.pin4, J11.pin4, J12.pin4, C8.2, C9.2
  N2: J2.pin1, D2.anode
  12V: D1.anode, Part3.N$8, Part4.N$8, D2.cathode, IC2.pin5, C5.+, IC3.pin6, IC4.pin6, IC5.pin6, IC6.pin6, IC7.pin6, IC8.pin6, IC9.pin6, IC10.pin6
  CAN H: R1.Pin_0, IC1.pin7, Part3.N$1, Part4.N$1
  N3: R1.Pin_1, J4.pin2
  CAN L: R2.Pin_0, IC1.pin6, Part3.N$2, Part4.N$2
  N4: R2.Pin_1, J3.pin2
  N5: J3.pin1, J4.pin1, C1.2
  CAN TX: IC1.pin1, TTGO-T7_V1_3.IO_05
  3.3V: IC1.pin3, C2.1, C3.+, U2.VCC, RR1.1, C6.1, TTGO-T7_V1_3.3V3, U3.VCC, C7.1, U4.VCC, U5.VCC, RR2.1, C8.1, C9.1
  CAN RX: IC1.pin4, TTGO-T7_V1_3.IO_04
  N6: Part3.N$4, Part4.N$4
  N7: Part3.N$7, Part4.N$7
  5V: IC2.pin1, C4.+, L1.2, TTGO-T7_V1_3.+5V
  N8: IC2.pin7, L1.1, D3.cathode
  Points1A: U2.1A, RR1.2, J5.pin5
  N9: U2.1B, U2.2Y
  Sense 1: U2.1Y, U2.2A, TTGO-T7_V1_3.IO_34
  Points1B: U2.2B, RR1.3, J5.pin3
  N10: U2.3Y, U2.4A
  Points2A: U2.3A, RR1.4, J6.pin5
  Sense 2: U2.3B, U2.4Y, TTGO-T7_V1_3.IO_35
  Points2B: U2.4B, RR1.5, J6.pin3
  Motor 2: IC3.pin2, IC3.pin4, TTGO-T7_V1_3.IO_02
  N11: IC3.pin5, J6.pin1
  N12: IC3.pin7, J6.pin2
  Motor 1: IC4.pin2, IC4.pin4, TTGO-T7_V1_3.IO_00
  N13: IC4.pin5, J5.pin1
  N14: IC4.pin7, J5.pin2
  Points 3A: RR1.6, U3.1A, J7.pin5
  Points 3B: RR1.7, U3.2B, J7.pin3
  Points 4A: RR1.8, U3.3A, J8.pin5
  Points 4B: RR1.9, U3.4B, J8.pin3
  Sense 3: TTGO-T7_V1_3.IO_36, U3.1Y, U3.2A
  Sense 4: TTGO-T7_V1_3.IO_39, U3.3B, U3.4Y
  Sense 7: TTGO-T7_V1_3.IO_26
  Motor 5: TTGO-T7_V1_3.IO_18, IC8.pin2, IC8.pin4
  Motor 8: TTGO-T7_V1_3.IO_33
  Motor 6: TTGO-T7_V1_3.IO_19, IC7.pin2, IC7.pin4
  Sense 5: TTGO-T7_V1_3.IO_23, U4.1Y, U4.2A
  Sense 8: TTGO-T7_V1_3.IO_27
  Sense 6: TTGO-T7_V1_3.IO_25
  Motor 7: TTGO-T7_V1_3.IO_32
  Motor 4: TTGO-T7_V1_3.IO_17, IC6.pin2, IC6.pin4
  Motor 3: TTGO-T7_V1_3.IO_16, IC5.pin2, IC5.pin4
  N15: U3.1B, U3.2Y
  N16: U3.3Y, U3.4A
  N17: IC5.pin5, J7.pin1
  N18: IC5.pin7, J7.pin2
  N19: IC6.pin5, J8.pin1
  N20: IC6.pin7, J8.pin2
  Points5A: U4.1A, RR2.2, J10.pin5
  N21: U4.1B, U4.2Y
  Points5B: U4.2B, RR2.3, J10.pin3
  N22: U4.3Y, U4.4A
  N23: U4.3B, U4.4Y
  N24: U5.1B, U5.2Y
  N25: U5.1Y, U5.2A
  N26: U5.3Y, U5.4A
  N27: U5.3B, U5.4Y
  N28: IC7.pin5, J9.pin1
  N29: IC7.pin7, J9.pin2
  N30: IC8.pin5, J10.pin1
  N31: IC8.pin7, J10.pin2
  N32: IC9.pin2, IC9.pin4
  N33: IC9.pin5, J11.pin1
  N34: IC9.pin7, J11.pin2
  N35: IC10.pin2, IC10.pin4
  N36: IC10.pin5, J12.pin1
  N37: IC10.pin7, J12.pin2

custom parts:
  Resistor: A generic 5-band resistor (0.25W)
  74HCT00: Quad 2-in NAND gates
  DIP - 8 pins: A DIP stand-in part for whatever IC you want. With 8 pins on a 300mil dual inline package (DIP) footprint.
