# Fritzing sketch SimpleIOCape (saved by Fritzing 0.9.6b)

parts:
  J2 = shrouded pin header, 10 pins [form="♂ (shrouded male)"]
  J1 = shrouded pin header, 10 pins [form="♂ (shrouded male)"]
  Part1 = Adafruit BeagleBone Proto Cape [part_number="Adafruit #572"]

nets:
  N1: J2.pin1, Part1.EHRPWM1A, Part1.4#174, Part1.4#196
  N2: J2.pin2, Part1.EHRPWM1B, Part1.5#175, Part1.5#197
  N3: J2.pin3, Part1.6#176, Part1.6#198
  N4: J2.pin4, Part1.GPIO_69, Part1.7#177, Part1.7#199
  N5: J2.pin5, Part1.GPIO_68, Part1.8#178, Part1.8#200
  N6: J2.pin6, Part1.GPIO_67, Part1.8#145, Part1.8#167
  N7: J2.pin7, Part1.GPIO_66, Part1.7#144, Part1.7#166
  N8: J2.pin8, J1.pin8, Part1.3.3V, Part1.6#143, Part1.6#165, Part1.6#242, Part1.6#264
  N9: J2.pin9, Part1.GPIO_48, Part1.5#142, Part1.5#164
  N10: J2.pin10, Part1.GPIO_60, Part1.4#141, Part1.4#163
  N11: J1.pin1, Part1.GPIO_115, Part1.4#106, Part1.4#273
  N12: J1.pin2, Part1.GPIO_112, Part1.5#107, Part1.5#274
  N13: J1.pin3, Part1.6#108, Part1.GND, Part1.6#275
  N14: J1.pin4, Part1.GPIO_47, Part1.7#109, Part1.7#276
  N15: J1.pin5, Part1.GPIO_46, Part1.8#110, Part1.8#277
  N16: J1.pin6, Part1.GPIO_44, Part1.8#244, Part1.8#266
  N17: J1.pin7, Part1.GPIO_45, Part1.7#243, Part1.7#265
  N18: J1.pin9, Part1.GPIO_117, Part1.5#241, Part1.5#263
  N19: J1.pin10, Part1.GPIO_49, Part1.4#240, Part1.4#262

custom parts:
  Adafruit BeagleBone Proto Cape: Add some circuitry to your Beagle Bone or Beagle Bone Black with our lovely Proto Cape. If you have a 'Bone you need one of these! This PCB fits neatly on top of a Beagle Bone, without getting in the way of the Ethernet jack, and provides a breakout to both 46 pin headers - with individual numbering to keep them straight. We also threw down some strips to access the 5V and 3V power supplies as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
