# Fritzing sketch RSFFDebounce (saved by Fritzing 0.9.5d)

parts:
  proto1 = adafruit
  IC1 = IC, DIP package, 14 pins [chip_label=7400]
  R1 = Resistor [tolerance=±5% resistance=10k package=THT]
  R2 = Resistor [tolerance=±5% resistance=10k package=THT]
  R3 = Resistor [tolerance=±5% resistance=10k package=THT]
  R4 = Resistor [tolerance=±5% resistance=10k package=THT]
  J1 = screw terminal, 8 pins
  C1 = Ceramic Capacitor [capacitance=100nF package="100 mil [THT, multilayer]"]

nets:
  N1: proto1.connectorA3, proto1.connectorA11
  N2: proto1.connectorA8, proto1.connectorX8
  N3: proto1.connectorA15, proto1.connectorW15
  N4: proto1.connectorB4, proto1.connectorB5
  N5: proto1.connectorC2, proto1.connectorC7
  N6: proto1.connectorD4, proto1.connectorE9
  N7: proto1.connectorD6, proto1.connectorD12
  N8: proto1.connectorD13, proto1.connectorI7
  N9: proto1.connectorD14, proto1.connectorJ3
  N10: proto1.connectorE10, proto1.connectorI6
  N11: proto1.connectorG4, proto1.connectorG8
  N12: proto1.connectorH5, proto1.connectorH6
  N13: proto1.connectorJ2, proto1.connectorY2
  N14: proto1.connectorJ11, proto1.connectorY11
  N15: proto1.connectorJ12, proto1.connectorY12
  N16: proto1.connectorJ13, proto1.connectorY13
  N17: proto1.connectorJ14, proto1.connectorY14
  N18: proto1.connectorW1, proto1.connectorY1
  N19: proto1.connectorX15, proto1.connectorZ15
  N20: IC1.pin1, IC1.pin6
  N21: IC1.pin2, R3.Pin_1, J1.pin5
  N22: IC1.pin3, IC1.pin4, J1.pin7
  N23: IC1.pin5, R4.Pin_1, J1.pin4
  GND: IC1.pin7, J1.pin8, C1.0
  N24: IC1.pin8, IC1.pin12
  N25: IC1.pin9, R2.Pin_0, J1.pin3
  N26: IC1.pin10, IC1.pin11, J1.pin6
  N27: IC1.pin13, R1.Pin_0, J1.pin2
  5V: IC1.pin14, R1.Pin_1, R2.Pin_1, R3.Pin_0, R4.Pin_0, J1.pin1, C1.1
