# Fritzing sketch StallMotorDriver (saved by Fritzing 0.9.5d)
stripboards: 1

parts:
  IC1 = IC, DIP package, 8 pins [chip_label=TC4428]
  J1 = screw terminal, 5 pins

nets:
  N1: IC1.pin2, IC1.pin4, J1.pin1
  GND: IC1.pin3, J1.pin5
  N2: IC1.pin5, J1.pin3
  N3: IC1.pin6, J1.pin4
  N4: IC1.pin7, J1.pin2

notes:
  In M1 M2 + G
  This is a simple GPIO => Stall Motor driver circuit. Can be built on a cheap little solderable breadboard.
